// Logisim project D__Flip_Flop.circ as structural Verilog
module main (
  input  D,
  input  CLK,
  input  in_3,
  input  in_4,
  output Q,
  output not_Q,
  output out_7
);

  wire nand_1_out, nand_2_out, nand_3_out, nand_4_out, nand_5_out, nand_6_out, not_1_out, not_2_out;

  not not_1 (not_1_out, D);
  not not_2 (not_2_out, CLK);
  nand nand_1 (nand_1_out, D, CLK);
  nand nand_2 (nand_2_out, CLK, not_1_out);
  nand nand_3 (nand_3_out, nand_1_out, nand_4_out);
  nand nand_4 (nand_4_out, nand_3_out, nand_2_out);
  D_Flip_Flop d_flip_flop_1 (.clk(in_3), .d(in_4), .q(out_7));
  nand nand_5 (nand_5_out, nand_3_out, not_2_out);
  nand nand_6 (nand_6_out, not_2_out, nand_4_out);
  nand nand_7 (Q, nand_5_out, not_Q);
  nand nand_8 (not_Q, Q, nand_6_out);
endmodule

// VHDL entity D_Flip_Flop, as the project stores it:
library ieee;
use ieee.std_logic_1164.all;
use ieee.std_logic_arith.all;
use ieee.std_logic_unsigned.all;

entity D_Flip_Flop is
    port(
        clk : in std_logic;
        d : in std_logic;
        q : out std_logic
    );
end entity D_Flip_Flop;

architecture bhv of D_Flip_Flop is
begin
    process(clk)
    begin
        if(clk'event AND clk = '1') then
            q <= d;
        end if;
    end process;
end architecture bhv;
