// Logisim project D__Latch.circ as structural Verilog
module main (
  input  D,
  input  CLK,
  input  in_3,
  input  in_4,
  output x,
  output not_x,
  output out_7
);

  wire nand_1_out, nand_2_out, not_1_out;

  not not_1 (not_1_out, D);
  nand nand_1 (nand_1_out, D, CLK);
  nand nand_2 (nand_2_out, CLK, not_1_out);
  D_Latch d_latch_1 (.CLK(in_3), .D(in_4), .Q(out_7));
  nand nand_3 (x, nand_1_out, not_x);
  nand nand_4 (not_x, x, nand_2_out);
endmodule

// VHDL entity D_Latch, as the project stores it:
library ieee;
use ieee.std_logic_1164.all;
use ieee.std_logic_arith.all;
use ieee.std_logic_unsigned.all;

entity D_Latch is
    port(
        CLK : in std_logic;
        D : in std_logic;
        Q : out std_logic
    );
end entity D_Latch;

architecture bhv of D_Latch is
begin
    process(CLK, D)
    begin
        if(CLK = '1') then
            Q <= D;
        end if;
    end process;
end architecture bhv;
