// Logisim project JK__Flip_Flop.circ as structural Verilog
module main (
  input  preset,
  input  J,
  input  CLK,
  input  K,
  input  clear,
  input  in_6,
  input  in_7,
  input  in_8,
  input  in_9,
  input  in_10,
  output Q,
  output not_Q,
  output out_13,
  output out_14
);

  wire nand_1_out, nand_2_out;

  nand nand_1 (nand_1_out, not_Q, J, CLK);
  nand nand_2 (nand_2_out, CLK, K, Q);
  nand nand_3 (Q, nand_1_out, preset, not_Q);
  nand nand_4 (not_Q, Q, clear, nand_2_out);
  JK_Flip_Flop jk_flip_flop_1 (.clk(in_6), .j(in_7), .k(in_8), .clr(in_9), .set(in_10), .q(out_13), .not_q(out_14));
endmodule

// VHDL entity JK_Flip_Flop, as the project stores it:
library ieee;
use ieee.std_logic_1164.all;

entity JK_Flip_Flop is
    port(
        clk   : in  std_logic;
        j     : in  std_logic;
        k     : in  std_logic;
        clr   : in  std_logic;
        set   : in  std_logic;
        q     : out std_logic;
        not_q : out std_logic
    );
end entity JK_Flip_Flop;

architecture bhv of JK_Flip_Flop is
    signal q_internal : std_logic := '0';
begin
    process(clk, clr, set)
    begin
        if clr = '1' then
            q_internal <= '0';
        elsif set = '1' then
            q_internal <= '1';
        elsif rising_edge(clk) then
            if    (j = '1' and k = '0') then
                q_internal <= '1';
            elsif (j = '0' and k = '1') then
                q_internal <= '0';
            elsif (j = '1' and k = '1') then
                q_internal <= not q_internal;
            end if;
        end if;
    end process;

    q     <= q_internal;
    not_q <= not q_internal;
end architecture bhv;
