// Logisim project RS__Latch.circ as structural Verilog
module main (
  input  in_1,
  input  in_2,
  input  in_3,
  input  in_4,
  output out_5,
  output out_6,
  output out_7,
  output out_8
);

  nand nand_1 (out_5, in_1, out_6);
  nand nand_2 (out_6, out_5, in_2);
  RS_Latch rs_latch_1 (.R(in_3), .S(in_4), .Q(out_7), .not_Q(out_8));
endmodule

// VHDL entity RS_Latch, as the project stores it:
library ieee;
use ieee.std_logic_1164.all;
use ieee.std_logic_arith.all;
use ieee.std_logic_unsigned.all;

entity RS_Latch is
    port(
        R :in std_logic;
        S :in std_logic;
        Q :out std_logic;
        not_Q :out std_logic
    );
end entity RS_Latch;

architecture bhv of RS_Latch is
   signal q_reg : std_logic := '0';
begin
    process(R, S)
    begin
        if (S = '1' and R = '0') then
            q_reg <= '1';
        elsif (S = '0' and R = '1') then
            q_reg <= '0';
        elsif (S = '0' and R = '0') then
            null;
        else
            q_reg <= 'X';
        end if;
    end process;

    Q     <= q_reg;
    not_Q <= not q_reg;
end architecture bhv;
